// Logisim project x XOR y.circ as structural Verilog: 1 circuit, main circuit main
module main (
  input  x,
  input  y,
  output x_XOR_y
);

  wire not_x_out, not_y_out, x_and_not_y_out, y_and_not_x_out;

  not not_x (not_x_out, x);
  not not_y (not_y_out, y);
  and y_and_not_x (y_and_not_x_out, not_x_out, y);
  and x_and_not_y (x_and_not_y_out, x, not_y_out);
  or or_1 (x_XOR_y, y_and_not_x_out, x_and_not_y_out);
endmodule
